# Fritzing sketch 7seg_button (saved by Fritzing 0.6.5b)
breadboards: 1

parts:
  7_Segment1 = 7 Segment Display
  S1 = Pushbutton [package="[THT]"]
  R6 = Resistor [tolerance=±5% resistance=330 package=THT]
  R7 = Resistor [tolerance=±5% resistance=330 package=THT]
  R8 = Resistor [tolerance=±5% resistance=330 package=THT]
  R9 = Resistor [tolerance=±5% resistance=330 package=THT]
  R10 = Resistor [tolerance=±5% resistance=330 package=THT]
  R12 = Resistor [tolerance=±5% resistance=330 package=THT]
  Arduino1 = Arduino
  R14 = Resistor [tolerance=±5% resistance=330 package=THT]
  R15 = Resistor [tolerance=±5% resistance=330 package=THT]

nets:
  N1: 7_Segment1.Segment_E, R7.Pin_1
  N2: 7_Segment1.Segment_D, R10.Pin_1
  N3: 7_Segment1.common_anode, Arduino1.+5V
  N4: 7_Segment1.Segment_C, R6.Pin_0
  N5: 7_Segment1.Segment_DP, R14.Pin_1
  N6: 7_Segment1.Segment_B, 7_Segment1.Segment_A, R12.Pin_0, Arduino1.D4, R15.Pin_0, R15.Pin_1
  N7: 7_Segment1.Segment_F, 7_Segment1.Segment_G, R8.Pin_1, R9.Pin_1
  N8: S1.Pin_1, S1.Pin_2, Arduino1.D2, R14.Pin_0
  N9: S1.Pin_3, S1.Pin_4, Arduino1.GND
  N10: R6.Pin_1, Arduino1.D5
  N11: R7.Pin_0, Arduino1.D7
  N12: R8.Pin_0, Arduino1.D9
  N13: R9.Pin_0, Arduino1.D8
  N14: R10.Pin_0, Arduino1.D6
  N15: R12.Pin_1, Arduino1.D3
