# Fritzing sketch Roomba (saved by Fritzing 0.7.0b)
breadboards: 1

parts:
  U1 = Arduino Mega
  Ultra_sound_sensor1 = ultrasound_sensor
  Ultra_sound_sensor2 = ultrasound_sensor
  Ultra_sound_sensor3 = ultrasound_sensor
  SerLCD_2_5_Module_hooked_to_a_16x2_LCD1 = SerLCD 2.5 16x2
  Arduino_micro_SD_module1 = Arduino_microsd
  パーツ1 = Real Time Clock Module - DS1307 RTC Breakout Board
  CN1 = DB9_rt_female

nets:
  N1: U1.D13, Arduino_micro_SD_module1.aún_sin_nombre#1
  N2: U1.D12, Arduino_micro_SD_module1.aún_sin_nombre#2
  N3: U1.D11, Arduino_micro_SD_module1.aún_sin_nombre#3
  N4: U1.D10, Arduino_micro_SD_module1.aún_sin_nombre#4
  N5: U1.D4, CN1.4_DTR
  N6: U1.D3, CN1.2_RXD
  N7: U1.D2, CN1.3_TXD
  5V: U1.+5V, Ultra_sound_sensor1.aún_sin_nombre#5, SerLCD_2_5_Module_hooked_to_a_16x2_LCD1.5V, Arduino_micro_SD_module1.aún_sin_nombre#6, パーツ1.5V
  GND: U1.GND, Ultra_sound_sensor1.aún_sin_nombre#6, Ultra_sound_sensor2.aún_sin_nombre#6, Ultra_sound_sensor3.aún_sin_nombre#6, SerLCD_2_5_Module_hooked_to_a_16x2_LCD1.GND, Arduino_micro_SD_module1.aún_sin_nombre#0, パーツ1.GND, CN1.5_GND
  N8: U1.A0, Ultra_sound_sensor1.aún_sin_nombre#2
  N9: U1.A1, Ultra_sound_sensor2.aún_sin_nombre#2
  N10: U1.A2, Ultra_sound_sensor3.aún_sin_nombre#2
  N11: U1.D18, SerLCD_2_5_Module_hooked_to_a_16x2_LCD1.RX
  N12: U1.D20, パーツ1.SDA
  N13: U1.D21, パーツ1.SCL
  N14: Ultra_sound_sensor2.aún_sin_nombre#5, Ultra_sound_sensor3.aún_sin_nombre#5
  N15: Arduino_micro_SD_module1.aún_sin_nombre#10, Arduino_micro_SD_module1.aún_sin_nombre#13
  N16: Arduino_micro_SD_module1.aún_sin_nombre#11, Arduino_micro_SD_module1.aún_sin_nombre#14, Arduino_micro_SD_module1.aún_sin_nombre#16, Arduino_micro_SD_module1.aún_sin_nombre#18, Arduino_micro_SD_module1.aún_sin_nombre#20
  N17: Arduino_micro_SD_module1.aún_sin_nombre#12, Arduino_micro_SD_module1.aún_sin_nombre#15, Arduino_micro_SD_module1.aún_sin_nombre#17, Arduino_micro_SD_module1.aún_sin_nombre#19, Arduino_micro_SD_module1.aún_sin_nombre#21

custom parts:
  SerLCD 2.5 16x2: A standard character display, usually with 2x16 characters. Comes in many colors.
  Arduino_microsd: Arduino MicroSD module is a small shield that you can connect to your Arduino board, once the shield is connected, you add SD flash memory to Arduino.
  DB9_rt_female: RS232 connector, 9 pin, right-angle female. Minimum connections are RXD, TXD,GND
